// Logisim project DL LAB1.circ as structural Verilog: 1 circuit, main circuit main
module main (
  input  A,
  input  A_2,
  input  B,
  input  B_2,
  input  A_3,
  input  A_4,
  input  B_3,
  input  B_4,
  input  A_5,
  output Y_A_prime_B_AB_prime,
  output Y_AB,
  output Y_A_B,
  output Y_AB_A_prime_B_prime,
  output Y_A_prime
);

  and AND (Y_AB, A_2, B_2);
  or OR (Y_A_B, A_3, B_3);
  not not_1 (Y_A_prime, A_5);
  xor XOR (Y_A_prime_B_AB_prime, A, B);
  xnor XNOR (Y_AB_A_prime_B_prime, A_4, B_4);

  // Notes on the sheet:
  //   NOT
endmodule
