// Logisim project DL LAB10.circ as structural Verilog: 1 circuit, main circuit main
module main (
  input  A,
  input  B,
  input  Bin,
  output Difference,
  output Bout
);

  wire and_1_out, and_2_out, not_1_out, not_2_out, xor_1_out;

  xor xor_1 (xor_1_out, A, B);
  not not_1 (not_1_out, xor_1_out);
  not not_2 (not_2_out, A);
  and and_1 (and_1_out, not_1_out, Bin);
  and and_2 (and_2_out, not_2_out, B);
  xor xor_2 (Difference, xor_1_out, Bin);
  or or_1 (Bout, and_1_out, and_2_out);
endmodule
