// Logisim project DL LAB3.circ as structural Verilog: 1 circuit, main circuit main
module main (
  input  A,
  input  A_2,
  input  B,
  input  A_3,
  input  B_2,
  output A_B,
  output A_prime,
  output A_B_2
);

  wire nor_2_out, nor_3_out, nor_5_out;

  nor nor_1 (A_prime, A_2, A_2);
  nor nor_2 (nor_2_out, A_3, A_3);
  nor nor_3 (nor_3_out, B_2, B_2);
  nor nor_4 (A_B_2, nor_2_out, nor_3_out);
  nor nor_5 (nor_5_out, A, B);
  nor nor_6 (A_B, nor_5_out, nor_5_out);
endmodule
